# Fritzing sketch Sketch_SmrtMultiTab (saved by Fritzing 0.9.3b)
breadboards: 1

parts:
  U1 = NodeMCU V1.0
  Part1 = KY-015 Temperature & Humidity Sensor Module [package="Breakout board"]
  Part2 = KY-019 5V Relay Module [package="Breakout board"]

nets:
  N1: U1.D4, Part2.S
  N2: U1.3V3, Part1.S, Part2.+
  N3: U1.GND, Part1.-, Part2.-
  N4: U1.D5, Part1.Vin

custom parts:
  NodeMCU V1.0: ESP8266 based NodeMCU
  KY-015 Temperature & Humidity Sensor Module: KY-015 temperature and humidity sensor module, provides a low-latency serial interface to measure humidity and temperature.
  KY-019 5V Relay Module: KY-019 5V Relay module, used to control AC circuits.
